# Fritzing sketch skull_arduino (saved by Fritzing 0.9.2b)
breadboards: 2

parts:
  Part1 = Arduino Uno (Rev3)
  JP2 = Header 11 [package=1x11_smd_no_holes]
  LED3 = LED - 5mm [color="Red (633nm)" package="5 mm [THT]"]
  LED4 = LED - 5mm [color="Red (633nm)" package="5 mm [THT]"]  # not connected
  S2 = Pushbutton [package="[THT]"]
  U2 = POT [package=pot_mammoth]
  R1 = Resistor [tolerance=±5% resistance=10k package=THT]
  R2 = Resistor [tolerance=±5% resistance=470 package=THT]
  R3 = Resistor [tolerance=±5% resistance=470 package=THT]

nets:
  N1: Part1.A1, JP2.2, U2.A
  N2: Part1.D9_PWM, JP2.9
  N3: Part1.GND, JP2.1, U2.S, R1.Pin_1, R2.Pin_1, R3.Pin_1
  N4: Part1.D2, JP2.5, JP2.7, S2.Pin_1, S2.Pin_2, R1.Pin_0
  N5: Part1.D6_PWM, JP2.11, LED3.anode
  N6: Part1.5V, JP2.3, JP2.4, JP2.6, S2.Pin_3, S2.Pin_4, U2.E
  N7: JP2.8, R2.Pin_0
  N8: JP2.10, LED3.cathode, R3.Pin_0

notes:
  Skull routing
